# Fritzing sketch raspberry-pi-gpio (saved by Fritzing 0.9.4)
circuit board: 6.88566cm x 5.36311cm
breadboards: 1

parts:
  R3 = Resistor [tolerance=±5% resistance=100k package=THT]
  Button = Pushbutton [package=THT]
  Raspberry_Pi_1 = Raspberry Pi 3 [part_number=RPI-3-V1.2]
  Mod1 = KY-019 5V Relay Module [package="Breakout board"]

nets:
  N1: R3.Pin_0, Button.leg1, Raspberry_Pi_1.GIPO5
  N2: R3.Pin_1, Raspberry_Pi_1.5V, Mod1.+
  N3: Button.leg0, Raspberry_Pi_1.GND, Mod1.-
  N4: Raspberry_Pi_1.GIPO4, Mod1.S

notes:
  FLIP FLOP

custom parts:
  KY-019 5V Relay Module: KY-019 5V Relay module, used to control AC circuits. (Special thanks to vanepp for fixing the PCB holes and other errors)

// code stored in the sketch: FlipFlop.ino
/*
  Flip Flop
  switching between two LEDs using a button
  
  This example is part of the Fritzing Creator Kit: www.fritzing.org/creator-kit.
*/

int buttonPin=2;                       // Pin where the button is attached
int greenLED=9;                        // Pin where the green LED is attached
int redLED=10;                         // Pin where the red LED is attached 

void setup(){
  pinMode(buttonPin, INPUT);           // button is initialised as INPUT 
  pinMode(greenLED, OUTPUT);           // green LED pin is initialised as OUTPUT 
  pinMode(redLED, OUTPUT);             // red LED pin is initialised as OUTPUT  
}

void loop(){
  if (digitalRead(buttonPin)==LOW){    // if the button is pressed (LOW) 
    digitalWrite(greenLED, HIGH);      // switch on green LED
    digitalWrite(redLED, LOW);         // switch off red LED
  } else {                             // else (if button is not pressed)
    digitalWrite(greenLED, LOW);       // switch off green LED
    digitalWrite(redLED, HIGH);        // switch on red LED
  }
}
